# Fritzing sketch laser_timer_7_segs (saved by Fritzing 0.9.0b)
breadboards: 2

parts:
  Part1 = Arduino Nano (Rev3.0)
  LED1 = 7-SEGMENT-4DIGIT [package=7-segment-4digit]
  R2 = Photocell (LDR) [package=THT]
  R01 = Resistor [tolerance=±5% resistance=220 package=THT]
  R03 = Resistor [tolerance=±5% resistance=220 package=THT]
  R02 = Resistor [tolerance=±5% resistance=220 package=THT]
  R05 = Resistor [tolerance=±5% resistance=220 package=THT]
  R04 = Resistor [tolerance=±5% resistance=220 package=THT]
  R10 = Resistor [tolerance=±5% resistance=220 package=THT]
  R07 = Resistor [tolerance=±5% resistance=220 package=THT]
  R11 = Resistor [tolerance=±5% resistance=220 package=THT]
  R_SENS = Resistor [tolerance=±5% resistance=1k package=THT]

nets (from the breadboard view):
  N1: Part1.GND, R_SENS.Pin_1
  N2: Part1.D2, R11.Pin_0
  N3: Part1.D3, R07.Pin_0
  N4: Part1.D4, R04.Pin_0
  N5: Part1.D5, R02.Pin_0
  N6: Part1.D6, R01.Pin_0
  N7: Part1.D7, R10.Pin_0
  N8: Part1.D8, R05.Pin_0
  N9: Part1.5V, R2.pin_0
  N10: Part1.A5, LED1.13
  N11: Part1.A4, LED1.11
  N12: Part1.A3, LED1.6
  N13: Part1.A2, R03.Pin_0
  N14: Part1.A1, LED1.16
  N15: Part1.A0, R2.pin_1, R_SENS.Pin_0
  N16: LED1.1, R01.Pin_1
  N17: LED1.2, R02.Pin_1
  N18: LED1.3, R03.Pin_1
  N19: LED1.4, R04.Pin_1
  N20: LED1.5, R05.Pin_1
  N21: LED1.9, R07.Pin_1
  N22: LED1.14, R10.Pin_1
  N23: LED1.15, R11.Pin_1
